# Fritzing sketch Design_Wirring (saved by Fritzing 0.9.3b)

parts:
  Raspberry_Pi_3 = Raspberry Pi 3 [part_number=RPI-3-V1.2]
  Sensor_Down = Soil Moisture Sensor
  220V = 220v plug
  MCB = SWITCH-MOMENTARY-2 [package=tactile-switch-1101ne]
  PSU = prefix0000 [part_number=S-350-60]
  RELAY = RELAY [package=relay-jzc]
  PL_1 = smd LED [color="Red (633nm)" package="0603 [SMD]"]
  MANUAL_UP = SWITCH-MOMENTARY-2 [package=tactile-switch-1101ne]
  MANUAL_DOWN = SWITCH-MOMENTARY-2 [package=tactile-switch-1101ne]
  Sensor_Up = Soil Moisture Sensor
  Raspberry_Pi_3_2 = Raspberry Pi 3 [part_number=RPI-3-V1.2]
  220V_2 = 220v plug
  PSU_2 = prefix0000 [part_number=S-350-60]
  MANUAL_DOWN_2 = SWITCH-MOMENTARY-2 [package=tactile-switch-1101ne]
  MANUAL_UP_2 = SWITCH-MOMENTARY-2 [package=tactile-switch-1101ne]
  MCB_2 = SWITCH-MOMENTARY-2 [package=tactile-switch-1101ne]
  RELAY_2 = RELAY [package=relay-jzc]
  PL_1_2 = smd LED [color="Red (633nm)" package="0603 [SMD]"]
  VLD_UP = SWITCH-MOMENTARY-2 [package=tactile-switch-1101ne]
  VLD_DOWN = SWITCH-MOMENTARY-2 [package=tactile-switch-1101ne]

nets:
  GND: Raspberry_Pi_3.GND, Sensor_Down.GND, PSU.connector5, RELAY.COIL2, PL_1.cathode, MANUAL_UP.1, MANUAL_DOWN.1, Sensor_Up.GND
  N1: Raspberry_Pi_3.GIPO13, Sensor_Down.SIG
  N2: Raspberry_Pi_3.GIPO19, Sensor_Up.SIG
  N3: Raspberry_Pi_3.GIPO25, RELAY.COIL1
  N4: Raspberry_Pi_3.GIPO24, MANUAL_DOWN.2
  N5: Raspberry_Pi_3.GIPO23, MANUAL_UP.2
  VCC: Raspberry_Pi_3.5V, Sensor_Down.VCC, PSU.connector0, RELAY.MAIN, Sensor_Up.VCC
  N6: 220V.pin1, PSU.connector7
  N7: 220V.pin2, MCB.1
  N8: MCB.2, PSU.connector8
  N9: RELAY.NO, PL_1.anode
  N10: Raspberry_Pi_3_2.GND, PSU_2.connector5, MANUAL_DOWN_2.1, MANUAL_UP_2.1, RELAY_2.COIL2, PL_1_2.cathode, VLD_UP.1, VLD_DOWN.1
  N11: Raspberry_Pi_3_2.GIPO13, VLD_UP.2
  N12: Raspberry_Pi_3_2.GIPO19, VLD_DOWN.2
  N13: Raspberry_Pi_3_2.GIPO25, RELAY_2.COIL1
  N14: Raspberry_Pi_3_2.GIPO24, MANUAL_DOWN_2.2
  N15: Raspberry_Pi_3_2.GIPO23, MANUAL_UP_2.2
  N16: Raspberry_Pi_3_2.5V, PSU_2.connector0, RELAY_2.MAIN
  N17: 220V_2.pin1, PSU_2.connector7
  N18: 220V_2.pin2, MCB_2.1
  N19: PSU_2.connector8, MCB_2.2
  N20: RELAY_2.NO, PL_1_2.anode

notes:
  Input
  Output

custom parts:
  220v plug: Generic 220V AC plug.
